// Logisim project odev.circ as structural Verilog: 1 circuit, main circuit main
module main (
  input  b,
  input  c,
  input  d,
  output f
);

  wire nand_1_out, nand_2_out, nand_3_out;

  nand nand_1 (nand_1_out, c, c);
  nand nand_2 (nand_2_out, nand_1_out, d);
  nand nand_3 (nand_3_out, b, b);
  nand nand_4 (f, nand_2_out, nand_3_out);
endmodule
