// Logisim project hw4.circ as structural Verilog: 1 circuit, main circuit main
module main (
  input  [3:0] A,
  input  y,
  input  [3:0] B,
  input  [3:0] C,
  input  x,
  output [3:0] Z
);

  wire [3:0] multiplexer_1_out, multiplexer_2_out, not_1_out;

  assign not_1_out = ~C;  // NOT_Gate not_1, 4 bits wide
  Multiplexer #(.width(4), .enable("false")) multiplexer_1 (.in0(B), .in1(A), .out(multiplexer_1_out), .sel(y));
  Multiplexer #(.width(4), .enable("false")) multiplexer_2 (.in0(A), .in1(not_1_out), .out(multiplexer_2_out), .sel(x));
  Adder #(.width(4)) adder_1 (.a(multiplexer_1_out), .b(multiplexer_2_out), .out(Z), .cin(x));  // open: cout

  // Notes on the sheet:
  //   1
  //   BLG 231E HW4
  //   Mustafa Can Çalışkan
  //   150200097
  //   4-bit 2:1 MUX
  //   3
  //   B
  //   A
  //   4
  //   4-bit 2:1 MUX
  //   A
  //   4
  //   C'
  //   4-bit parallel adder
  //   2
endmodule
